// Logisim project Domaci_zad.circ as structural Verilog: 1 circuit, main circuit main
module main (
  input  X1,
  input  X2,
  input  X3,
  input  X4,
  output Y
);

  wire not_1_out, not_2_out, not_3_out, not_4_out, not_5_out, or_1_out, or_2_out, or_3_out;

  not not_1 (not_1_out, X1);
  not not_2 (not_2_out, X3);
  not not_3 (not_3_out, X2);
  not not_4 (not_4_out, X1);
  not not_5 (not_5_out, X3);
  or or_1 (or_1_out, not_1_out, X2, not_2_out);
  or or_2 (or_2_out, not_3_out, X3);
  or or_3 (or_3_out, not_4_out, not_5_out, X4);
  and and_1 (Y, or_1_out, or_2_out, or_3_out);
endmodule
